# Fritzing sketch schema (saved by Fritzing 0.9.4)
circuit board: 8.636cm x 6.11011cm
breadboards: 1

parts:
  S1 = Momentary Switch [package=ksa_sealed_tac_switch]
  S3 = Momentary Switch [package=ksa_sealed_tac_switch]
  R1 = Resistor [tolerance=±5% resistance=220 package="0603 [SMD]"]
  R2 = Resistor [tolerance=±5% resistance=220 package="0603 [SMD]"]
  R3 = Resistor [tolerance=±5% resistance=220 package="0603 [SMD]"]
  LED3 = smd LED [color="Red (633nm)" package="0805 [SMD]"]
  LED4 = smd LED [color="Blue (430nm)" package="0805 [SMD]"]
  RTC_DS1302 = RTC_DS1302_module
  Display_TS1637 = Grove 4 Digit Display
  LED5 = smd LED [color="Yellow (595nm)" package="0805 [SMD]"]
  S2 = Momentary Switch [package=ksa_sealed_tac_switch]
  Arduino = Arduino Nano (Rev3.0)

nets:
  Btn Inc: S1.1, Arduino.D10
  Vcc: S1.2, S3.2, RTC_DS1302.VCC, Display_TS1637.VCC, S2.2, Arduino.5V
  N1: S1.4, R1.Pin_1
  Btn Hgl: S3.1, Arduino.D8
  N2: S3.4, R3.Pin_1
  N3: R1.Pin_0, LED3.anode
  N4: R2.Pin_0, LED4.anode
  N5: R2.Pin_1, S2.4
  N6: R3.Pin_0, LED5.anode
  GRD: LED3.cathode, LED4.cathode, RTC_DS1302.GND, Display_TS1637.GND, LED5.cathode, Arduino.GND
  Rtc Reset: RTC_DS1302.RST, Arduino.D5
  Rtc Data: RTC_DS1302.DAT, Arduino.D6
  Rtc CLK: RTC_DS1302.CLK, Arduino.D7
  Disp IO: Display_TS1637.DIO, Arduino.D2
  Disp CLK: Display_TS1637.CLK, Arduino.D3
  Btn Mode: S2.1, Arduino.D9

custom parts:
  RTC_DS1302_module: Arduino module DS1302 SPI Real Time Clock
